# Fritzing sketch photoresistor-distance-sensor (saved by Fritzing 0.9.4)
breadboards: 1

parts:
  Part1 = Arduino Uno (Rev3)
  R1 = Photocell (LDR) [package=THT]
  HC-SR04_Sensor_1 = HC-SR04 Ultrasonic Distance Sensor
  R2 = Resistor [tolerance=±5% resistance=10k package=THT]

nets:
  GND: Part1.A0, Part1.GND, HC-SR04_Sensor_1.GND, R2.Pin_1
  N1: Part1.D11_PWM/MOSI, HC-SR04_Sensor_1.ECHO
  N2: Part1.D12/MISO, HC-SR04_Sensor_1.TRIG
  5V: Part1.5V, R1.pin_1, HC-SR04_Sensor_1.VCC
  N3: R1.pin_0, R2.Pin_0
