# Fritzing sketch tilt-led (saved by Fritzing 0.9.4)
breadboards: 1

parts:
  Part1 = Arduino Uno (Rev3)
  S1 = Tilt Switch [package=THT]
  R1 = Resistor [tolerance=±5% resistance=10k package=THT]
  LED1 = LED - 5mm [color="Orange (605nm)" package="5 mm [THT]"]

nets:
  N1: Part1.D3_PWM, LED1.anode
  N2: Part1.D7, S1.Pin_1, R1.Pin_1
  N3: Part1.5V, R1.Pin_0
  N4: Part1.GND, S1.Pin_2, LED1.cathode
