# Fritzing sketch distance-sensor-motor (saved by Fritzing 0.9.4)
breadboards: 1

parts:
  Part1 = Arduino Uno (Rev3)
  R1 = Resistor [tolerance=±5% resistance=330 package=THT]
  D1 = Rectifier Diode [part_number=1N4001 package="300 mil [THT]"]
  M1 = DC Motor
  HC-SR04_Sensor_1 = HC-SR04 Ultrasonic Distance Sensor
  Q1 = NPN-Transistor [package="TO92 [THT]"]
  R2 = Resistor [tolerance=±5% resistance=220 package=THT]
  LED1 = LED - 5mm [color="Red (633nm)" package="5 mm [THT]"]

nets:
  N1: Part1.D8, LED1.anode
  N2: Part1.D11_PWM/MOSI, HC-SR04_Sensor_1.ECHO
  N3: Part1.D12/MISO, HC-SR04_Sensor_1.TRIG
  N4: Part1.D6_PWM, R1.Pin_0
  5V: Part1.5V, D1.cathode, M1.pin_1, HC-SR04_Sensor_1.VCC
  GND: Part1.GND, HC-SR04_Sensor_1.GND, Q1.E, R2.Pin_1
  N5: R1.Pin_1, Q1.B
  N6: D1.anode, M1.pin_2, Q1.C
  N7: R2.Pin_0, LED1.cathode
