# Fritzing sketch distance-sensor (saved by Fritzing 0.9.4)
breadboards: 1

parts:
  Part1 = Arduino Uno (Rev3)
  HC-SR04_Sensor_1 = HC-SR04 Ultrasonic Distance Sensor

nets:
  N1: Part1.D11_PWM/MOSI, HC-SR04_Sensor_1.ECHO
  N2: Part1.D12/MISO, HC-SR04_Sensor_1.TRIG
  5V: Part1.5V, HC-SR04_Sensor_1.VCC
  GND: Part1.GND, HC-SR04_Sensor_1.GND
