# Fritzing sketch photoresistor-servo (saved by Fritzing 0.9.3b)
breadboards: 1

parts:
  Part1 = Arduino Uno (Rev3)
  R1 = Resistor [tolerance=±5% resistance=220 package=THT]
  R2 = Photocell (LDR) [package=THT]
  J1 = Basic Servo

nets:
  5V: Part1.A0, Part1.5V, R1.Pin_1, R2.pin_0, J1.vcc
  N1: Part1.D9_PWM, J1.pulse
  GND: Part1.GND, R1.Pin_0, R2.pin_1, J1.gnd
