# Fritzing sketch photo-buzzer-button-servo (saved by Fritzing 0.9.4)
breadboards: 1

parts:
  Part1 = Arduino Uno (Rev3)
  S1 = Round Pushbutton
  J1 = Basic Servo
  J2 = Piezo Speaker
  R1 = PHOTOCELL [package=photocell]
  R2 = Resistor [tolerance=±5% resistance=220 package="2512 [SMD]"]
  R3 = Resistor [tolerance=±5% resistance=10k package="2512 [SMD]"]

nets:
  N1: Part1.A0, R1.P$2, R3.Pin_1
  N2: Part1.D9_PWM, J1.pulse
  N3: Part1.D13/SCK, J2.pin2
  N4: Part1.D2, S1.leg1, R2.Pin_1
  5V: Part1.5V, J1.vcc, R1.P$1, R2.Pin_0
  GND: Part1.GND, S1.leg0, J1.gnd, J2.pin1, R3.Pin_0
