# Fritzing sketch DHT11-lcd-sketch (saved by Fritzing 0.9.4)
breadboards: 1

parts:
  Part1 = Arduino Uno (Rev3)
  U1 = LCD-16X2 [package=lcd-16x2]
  R1 = Rotary Potentiometer (Small) [maximum_resistance=100kΩ package=THT]
  R2 = Resistor [tolerance=±5% resistance=220 package=THT]
  Mod1 = KY-015 Temperature & Humidity Sensor Module [package="Breakout board"]

nets:
  N1: Part1.D11_PWM/MOSI, U1.E
  N2: Part1.D12/MISO, U1.RS
  N3: Part1.D2, U1.DB7
  N4: Part1.D3_PWM, U1.DB6
  N5: Part1.D4, U1.DB5
  N6: Part1.D5_PWM, U1.DB4
  N7: Part1.D7, Mod1.S
  5V: Part1.5V, U1.VDD, R1.leg2, R2.Pin_1, Mod1.Vin
  GND: Part1.GND, U1.VSS, U1.R_W, U1.K, R1.leg1, Mod1.-
  N8: U1.VO, R1.wiper
  N9: U1.A, R2.Pin_0

custom parts:
  KY-015 Temperature & Humidity Sensor Module: KY-015 temperature and humidity sensor module, provides a low-latency serial interface to measure humidity and temperature.
