# Fritzing sketch nightlight-circuit (saved by Fritzing 0.9.4)
breadboards: 1

parts:
  Part1 = Arduino Uno (Rev3)
  R1 = Resistor [tolerance=±5% resistance=220 package=THT]
  LED1 = LED - 5mm [color="Red (633nm)" package="5 mm [THT]"]
  R2 = Photocell (LDR) [package=THT]
  R3 = Resistor [tolerance=±5% resistance=220 package=THT]

nets:
  N1: Part1.A0, R2.pin_0, R3.Pin_0
  N2: Part1.D12/MISO, R1.Pin_1
  N3: Part1.5V, R2.pin_1
  N4: Part1.GND, LED1.cathode, R3.Pin_1
  N5: R1.Pin_0, LED1.anode
